# Fritzing sketch counter_board (saved by Fritzing 0.9.3b)
breadboards: 1

parts:
  Onderdeel1 = Arduino Uno (Rev3)
  R1 = Resistor [tolerance=±5% resistance=4.7k package=THT]
  U1 = attiny85 [package=dip]
  R2 = Resistor [tolerance=±5% resistance=4.7k package=THT]
  D2 = Rectifier Diode [part_number=1N4001 package="300 mil [THT]"]
  R5 = Resistor [tolerance=±5% resistance=220 package=THT]
  J2 = Screw terminal - 2 pins [package=THT]
  U2 = TLP621 [package=THT]
  U3 = TLP621 [package=THT]
  R6 = Resistor [tolerance=±5% resistance=220 package=THT]
  R7 = Resistor [tolerance=±5% resistance=220 package=THT]
  R8 = Resistor [tolerance=±5% resistance=220 package=THT]
  R9 = Resistor [tolerance=±5% resistance=220 package=THT]
  D3 = Zener Diode [part_number=1N4732A breakdown_voltage=3.6V package="300 mil [THT]"]
  C1 = Ceramic Capacitor [capacitance=100nF package="100 mil [THT, multilayer]"]
  Q1 = MOSFET-NCHANNEL [package=to220v]
  R10 = Resistor [tolerance=±5% resistance=220 package=THT]
  J3 = Screw terminal - 2 pins [package=THT]

nets:
  N1: Onderdeel1.A4/SDA, U1.Pin_5, R2.Pin_1
  N2: Onderdeel1.A5/SCL, R1.Pin_1, U1.Pin_7
  N3: Onderdeel1.5V, R1.Pin_0, U1.Pin_1, U1.Pin_8, R2.Pin_0, U2.Pin_4, U3.Pin_4
  GND: Onderdeel1.GND, U1.Pin_4, U1.Pin_6, U3.Pin_2, R6.Pin_1, R7.Pin_1, D3.anode, C1.0, Q1.S
  5V: Onderdeel1.VIN
  N4: U1.Pin_2, U2.Pin_3, R6.Pin_0
  N5: U1.Pin_3, U3.Pin_3, R7.Pin_0
  N6: D2.cathode, J2.pin2, U2.Pin_1
  N7: D2.anode, R5.Pin_1, U2.Pin_2
  N8: R5.Pin_0, J2.pin1
  N9: U3.Pin_1, Q1.D, R10.Pin_1
  N10: R8.Pin_0, J3.pin1
  N11: R8.Pin_1, R9.Pin_0, D3.cathode
  N12: R9.Pin_1, C1.1, Q1.G
  N13: R10.Pin_0, J3.pin2
